# Fritzing sketch Sketch (saved by Fritzing 1.0.6)
circuit board: 8.46667cm x 5.64444cm
breadboards: 1

parts:
  A1 = Esp32-c3 super mini
  RE1 = KY-040 Rotary encoder [package="Breakout board"]
  Squix1 = OLED 0.96" 128x64 I2C SSD1306  # not connected

nets:
  N1: A1.Pin_6, RE1.SW
  N2: A1.Pin_7, RE1.DT
  N3: A1.Pin_8, RE1.CLK
  N4: A1.Pin_14, RE1.Vcc
  N5: A1.Pin_15, RE1.GND

custom parts:
  Esp32-c3 super mini: ESP32-C3 Development Board ESP32 SuperMini Development Board ESP32 Development Board WiFi Bluetooth.
  KY-040 Rotary encoder: KY-040 Rotary Encoder with switch on breakout borad from AZ Delivery
